# Fritzing sketch brew_temp_v1 (saved by Fritzing 0.8.3b)
stripboards: 1

parts:
  Part1 = Arduino Uno (Rev3)
  LCD2 = LCD screen
  R2 = Trimmer Potentiometer [maximum_resistance=10kΩ package=THT]
  T1 = LM35 Temperature Sensor [package="TO92 [THT]"]
  T2 = LM35 Temperature Sensor [package="TO92 [THT]"]
  R3 = Resistor [tolerance=±5% resistance=4.7k package=THT]
  J1 = Piezo Speaker

nets:
  N1: Part1.ICSP_MISO, Part1.D12/MISO, T1.Vout, T2.Vout, R3.Pin_1
  GND: Part1.GND, LCD2.VSS, LCD2.R/W, LCD2.LED-, R2.leg1, R2.leg2, T1.+Vs, T1.GND, T2.+Vs, T2.GND
  N2: Part1.D8, LCD2.DB6
  N3: Part1.D9_PWM, LCD2.DB7
  N4: Part1.D11_PWM/MOSI, J1.pin2
  N5: Part1.D4, LCD2.RS
  N6: Part1.D5_PWM, LCD2.E
  N7: Part1.D6_PWM, LCD2.DB3, LCD2.DB4
  N8: Part1.D7, LCD2.DB5
  5V: Part1.5V, LCD2.VDD, LCD2.LED+, R3.Pin_0, J1.pin1
  N9: LCD2.V0, R2.wiper
